# Fritzing sketch fritzing (saved by Fritzing 0.9.10b)

parts:
  Part1 = Adafruit ADXL345 [part_number="Adafruit #1231"]
  MIC1 = MAX4466 Electret Microphone Breakout Board
  Power_plug1 = Power plug
  U1 = WS2812 RGB LED strip
  M1 = DOIT Esp32 DevKit v1 (30 pins long, 11 pins width) [part_number=ESP32S-PIN30]

nets:
  VIN: Part1.VIN, Power_plug1.VCC, U1.VCC, M1.VIN
  GND: Part1.GND, MIC1.GND, Power_plug1.GND, U1.GND, M1.GND
  N1: Part1.INT1, M1.RX2
  N2: Part1.SDA/SDIO, M1.D21
  N3: Part1.SCL, M1.D22
  N4: MIC1.out, M1.D15
  VCC: MIC1.VCC, M1.3V3
  N5: U1.DIN, M1.D12

custom parts:
  Adafruit ADXL345: Filling out our accelerometer offerings, we now have the really lovely digital ADXL345 from Analog Devices, a triple-axis accelerometer with digital I2C and SPI interface breakout. We added an on-board 3.3V regulator and logic-level shifting circuitry, making it a perfect choice for interfacing with any 3V or 5V microcontroller such as the Arduino. The sensor has three axes of measurements, X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
  MAX4466 Electret Microphone Breakout Board: MAX4466 Electrec Microphone Breakout Board
  WS2812 RGB LED strip: WS2812 strip
  DOIT Esp32 DevKit v1 (30 pins long, 11 pins width): The DOIT Esp32 DevKit v1 is one of the development board created by DOIT to evaluate the ESP-WROOM-32 module. It is based on the ESP32 microcontroller that boasts Wifi, Bluetooth, Ethernet and Low Power support all in a single chip. (vanepp) made breadboard work, adjusted pin numbering and labels and reduced size of schematic and cleaned up pcb. This chip is 30pins long (2 x15) and 11 pins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
